// Logisim project lab2.circ as structural Verilog: 2 circuits, main circuit main
module main (
  input  in_1,
  input  in_2,
  input  D0,
  input  D1,
  input  D2,
  input  D3,
  input  D4,
  input  D5,
  input  D6,
  input  D7,
  output out_11,
  output out_12,
  output out_13,
  output out_14,
  output out_15,
  output out_16,
  output out_17,
  output out_18,
  output out_19
);

  wire clock_1_out, nand_1_out, nand_2_out, nand_4_out;

  Clock clock_1 (.out(clock_1_out));
  nand nand_1 (nand_1_out, in_2, in_1);
  nand nand_2 (nand_2_out, nand_1_out, in_2);
  nand nand_3 (out_11, nand_1_out, nand_4_out);
  nand nand_4 (nand_4_out, out_11, nand_2_out);
  d_latch d_latch_1 (.in_1(D0), .in_2(clock_1_out), .out_3(out_12));
  d_latch d_latch_2 (.in_1(D1), .in_2(clock_1_out), .out_3(out_13));
  d_latch d_latch_3 (.in_1(D2), .in_2(clock_1_out), .out_3(out_14));
  d_latch d_latch_4 (.in_1(D3), .in_2(clock_1_out), .out_3(out_15));
  d_latch d_latch_5 (.in_1(D4), .in_2(clock_1_out), .out_3(out_16));
  d_latch d_latch_6 (.in_1(D5), .in_2(clock_1_out), .out_3(out_17));
  d_latch d_latch_7 (.in_1(D6), .in_2(clock_1_out), .out_3(out_18));
  d_latch d_latch_8 (.in_1(D7), .in_2(clock_1_out), .out_3(out_19));

  // Notes on the sheet:
  //   D
  //   CLK
endmodule

module d_latch (
  input  in_1,
  input  in_2,
  output out_3
);

  wire nand_1_out, nand_2_out, nand_4_out;

  nand nand_1 (nand_1_out, in_2, in_1);
  nand nand_2 (nand_2_out, nand_1_out, in_2);
  nand nand_3 (out_3, nand_1_out, nand_4_out);
  nand nand_4 (nand_4_out, out_3, nand_2_out);

  // Notes on the sheet:
  //   D
endmodule
